// Logisim project LA_MEA_MANO.circ as structural Verilog: 1 circuit, main circuit main
module main (
  input  A3,
  input  A2,
  input  A1,
  input  A0,
  output a,
  output b,
  output c,
  output d,
  output e,
  output f,
  output g
);

  wire and_1_out, and_2_out, and_3_out, and_4_out, and_5_out, and_6_out, and_7_out, and_8_out, and_9_out,
       and_10_out, and_11_out, and_12_out, and_13_out, and_14_out, and_15_out, and_16_out, and_17_out,
       and_18_out, and_19_out, and_20_out, and_21_out, and_22_out, and_23_out, and_24_out, and_25_out,
       and_26_out, and_27_out, and_28_out, and_29_out, and_30_out, and_31_out, not_1_out, not_2_out,
       not_3_out, not_4_out;

  not not_1 (not_1_out, A3);
  not not_2 (not_2_out, A2);
  not not_3 (not_3_out, A1);
  not not_4 (not_4_out, A0);
  and and_1 (and_1_out, not_1_out, not_2_out, not_4_out);
  and and_2 (and_2_out, A2, A0);
  and and_3 (and_3_out, A3, A0);
  and and_4 (and_4_out, A2, A1);
  and and_5 (and_5_out, not_1_out, A1);
  and and_6 (and_6_out, not_3_out, not_4_out);
  and and_7 (and_7_out, not_1_out, A2, not_3_out);
  and and_8 (and_8_out, A2, not_4_out);
  and and_9 (and_9_out, A3, not_2_out, A0);
  and and_10 (and_10_out, A1, not_4_out);
  and and_11 (and_11_out, not_1_out, not_2_out, A0);
  and and_12 (and_12_out, A3, not_3_out);
  and and_13 (and_13_out, not_1_out, not_2_out, not_4_out);
  and and_14 (and_14_out, not_2_out, A1);
  and and_15 (and_15_out, not_1_out, A2, not_3_out, A0);
  and and_16 (and_16_out, A1, not_4_out);
  and and_17 (and_17_out, A3, A2, not_4_out);
  and and_18 (and_18_out, A3, A1);
  and and_19 (and_19_out, A1, A0);
  and and_20 (and_20_out, A3, A0);
  and and_21 (and_21_out, not_1_out, A2, not_4_out);
  and and_22 (and_22_out, A3, not_2_out);
  and and_23 (and_23_out, not_1_out, not_3_out, not_4_out);
  and and_24 (and_24_out, not_1_out, A0);
  and and_25 (and_25_out, not_2_out, A1);
  and and_26 (and_26_out, A2, not_3_out);
  and and_27 (and_27_out, A3, not_4_out);
  and and_28 (and_28_out, not_2_out, not_4_out);
  and and_29 (and_29_out, A3, A1);
  and and_30 (and_30_out, not_1_out, A2, not_3_out);
  and and_31 (and_31_out, A3, A0);
  or or_1 (a, and_1_out, and_2_out, and_3_out, and_4_out, and_5_out);
  or or_2 (b, and_6_out, and_7_out, and_8_out, and_9_out);
  or or_3 (c, and_10_out, and_11_out, and_12_out);
  or or_4 (d, and_13_out, and_14_out, and_15_out, and_16_out, and_17_out, and_18_out);
  or or_5 (e, and_19_out, and_20_out, and_21_out, and_22_out, and_23_out);
  or or_6 (f, and_24_out, and_25_out, and_26_out, and_27_out);
  or or_7 (g, and_28_out, and_29_out, and_30_out, and_31_out);
endmodule
